# Fritzing sketch brazo_robot (saved by Fritzing 0.6.2b)
breadboards: 1

parts:
  Arduino1 = Arduino
  J1 = Basic Servo
  J2 = Basic Servo
  J3 = Basic Servo
  J4 = Basic Servo
  Q1 = NPN-Transistor [package="TO92 [THT]"]

nets:
  N1: Arduino1.D12, Q1.E
  N2: Arduino1.D6, J3.pulse
  N3: Arduino1.D5, J2.pulse
  N4: Arduino1.D3, J4.pulse
  VCC: Arduino1.+5V, J1.vcc, J2.vcc, J3.vcc, J4.vcc, Q1.B
  GND: Arduino1.GND, J1.gnd, J2.gnd, J3.gnd, J4.gnd, Q1.C

notes:
  Esto es el receptor IR tsop1736
